// Logisim project Computer.circ as structural Verilog
module main (
);

  wire clockunit_1_clock_out, dipswitch_1_sw1, dipswitch_1_sw2, mbcontrol_1_ald, mbcontrol_1_bld,
       mbcontrol_1_cld, mbcontrol_1_dld, txbcontrola_1_iald, txbcontrola_1_iatoe, txbcontrola_1_pcld,
       txbcontrola_1_pctoe, txbcontrola_1_spop, txbcontrola_1_spush, txbcontrola_1_txld, txbcontrola_1_txtoe,
       txbcontrolb_1_ald, txbcontrolb_1_aoh, txbcontrolb_1_aol, txbcontrolb_1_bld, txbcontrolb_1_boh,
       txbcontrolb_1_bol, txbcontrolb_1_cld, txbcontrolb_1_coh, txbcontrolb_1_col, txbcontrolb_1_dld,
       txbcontrolb_1_doh, txbcontrolb_1_dol, txbcontrolb_1_fld, txbcontrolb_1_foe, undriven_2, undriven_3,
       undriven_4, undriven_5, undriven_6, undriven_7;
  wire [2:0] undriven_8;
  wire [7:0] arithmeticlogicunit_1_flags_out, flagsregister_1_oflags, memoryunit_1_data_bus,
       pull_resistor_4_node, undriven, undriven_9;
  wire [15:0] addressregister_1_addr_bus, addressregister_1_tfer_buso;

  TXBControlA txbcontrola_1 (
    .TXBC(undriven), .TXLD(txbcontrola_1_txld), .IATOE(txbcontrola_1_iatoe), .IALD(txbcontrola_1_iald),
    .SPUSH(txbcontrola_1_spush), .SPOP(txbcontrola_1_spop), .PCTOE(txbcontrola_1_pctoe),
    .PCLD(txbcontrola_1_pcld), .TXTOE(txbcontrola_1_txtoe));
  DipSwitch #(.number(2)) dipswitch_1 (.sw1(dipswitch_1_sw1), .sw2(dipswitch_1_sw2));
  ClockUnit clockunit_1 (
    .MANUAL_CLOCK(dipswitch_1_sw1), .CLOCK_SELECT(dipswitch_1_sw2), .CLOCK_OUT(clockunit_1_clock_out));  // open: INV_CLOCK_OUT
  AddressRegister addressregister_1 (
    .TFER_BUS(addressregister_1_tfer_buso), .INC(undriven_5), .DEC(undriven_6), .OADDR(undriven_7),
    .OTFER(txbcontrola_1_pctoe), .Load(txbcontrola_1_pcld), .CLOCK(clockunit_1_clock_out),
    .ADDR_BUS(addressregister_1_addr_bus), .TFER_BUSO(addressregister_1_tfer_buso));
  AddressRegister addressregister_2 (
    .TFER_BUS(addressregister_1_tfer_buso), .OTFER(txbcontrola_1_txtoe), .Load(txbcontrola_1_txld),
    .CLOCK(clockunit_1_clock_out), .ADDR_BUS(addressregister_1_addr_bus),
    .TFER_BUSO(addressregister_1_tfer_buso));  // open: INC, DEC, OADDR
  AddressRegister addressregister_3 (
    .TFER_BUS(addressregister_1_tfer_buso), .OTFER(txbcontrola_1_iatoe), .Load(txbcontrola_1_iald),
    .CLOCK(clockunit_1_clock_out), .TFER_BUSO(addressregister_1_tfer_buso));  // open: INC, DEC, OADDR, ADDR_BUS
  MemoryUnit memoryunit_1 (
    .ADDR_BUS(addressregister_1_addr_bus), .RWB(undriven_4), .CLOCK(clockunit_1_clock_out),
    .DATA_BUS(memoryunit_1_data_bus));
  MemoryBridge memorybridge_1 (
    .LOAD(undriven_2), .STORE(undriven_3), .TFRL_BUS(addressregister_1_tfer_buso[7:0]),
    .DATA_BUS(memoryunit_1_data_bus), .ODATA_BUS(memoryunit_1_data_bus),
    .OTFRL_BUS(addressregister_1_tfer_buso[7:0]));
  Stack stack_1 (
    .TFER_BUS(addressregister_1_tfer_buso), .CLOCK(clockunit_1_clock_out), .PUSH(txbcontrola_1_spush),
    .POP(txbcontrola_1_spop), .OTFER_BUS(addressregister_1_tfer_buso));
  // Probe on memoryunit_1_data_bus
  Pull_Resistor pull_resistor_1 (.node(memoryunit_1_data_bus));
  // Probe on addressregister_1_addr_bus
  // Probe on addressregister_1_tfer_buso
  Pull_Resistor pull_resistor_2 (.node(addressregister_1_addr_bus));
  Pull_Resistor pull_resistor_3 (.node(addressregister_1_tfer_buso));
  // Probe on pull_resistor_4_node
  Pull_Resistor pull_resistor_4 (.node(pull_resistor_4_node));
  GeneralPurposeRegister generalpurposeregister_1 (
    .TFRL_BUS(addressregister_1_tfer_buso[7:0]), .TFRH_BUS(addressregister_1_tfer_buso[15:8]),
    .MAIN_BUS(pull_resistor_4_node), .TFRL(txbcontrolb_1_aol), .TFRH(txbcontrolb_1_aoh),
    .TXLD(txbcontrolb_1_ald), .CLOCK(clockunit_1_clock_out), .MBLD(mbcontrol_1_ald),
    .TFRH_BUSO(addressregister_1_tfer_buso[15:8]), .TFRL_BUSO(addressregister_1_tfer_buso[7:0]));
  GeneralPurposeRegister generalpurposeregister_2 (
    .TFRL_BUS(addressregister_1_tfer_buso[7:0]), .TFRH_BUS(addressregister_1_tfer_buso[15:8]),
    .MAIN_BUS(pull_resistor_4_node), .TFRL(txbcontrolb_1_bol), .TFRH(txbcontrolb_1_boh),
    .TXLD(txbcontrolb_1_bld), .CLOCK(clockunit_1_clock_out), .MBLD(mbcontrol_1_bld),
    .TFRH_BUSO(addressregister_1_tfer_buso[15:8]), .TFRL_BUSO(addressregister_1_tfer_buso[7:0]));
  GeneralPurposeRegister generalpurposeregister_3 (
    .TFRL_BUS(addressregister_1_tfer_buso[7:0]), .TFRH_BUS(addressregister_1_tfer_buso[15:8]),
    .MAIN_BUS(pull_resistor_4_node), .TFRL(txbcontrolb_1_col), .TFRH(txbcontrolb_1_coh),
    .TXLD(txbcontrolb_1_cld), .CLOCK(clockunit_1_clock_out), .MBLD(mbcontrol_1_cld),
    .TFRH_BUSO(addressregister_1_tfer_buso[15:8]), .TFRL_BUSO(addressregister_1_tfer_buso[7:0]));
  GeneralPurposeRegister generalpurposeregister_4 (
    .TFRL_BUS(addressregister_1_tfer_buso[7:0]), .TFRH_BUS(addressregister_1_tfer_buso[15:8]),
    .MAIN_BUS(pull_resistor_4_node), .TFRL(txbcontrolb_1_dol), .TFRH(txbcontrolb_1_doh),
    .TXLD(txbcontrolb_1_dld), .CLOCK(clockunit_1_clock_out), .MBLD(mbcontrol_1_dld),
    .TFRH_BUSO(addressregister_1_tfer_buso[15:8]), .TFRL_BUSO(addressregister_1_tfer_buso[7:0]));
  ArithmeticLogicUnit arithmeticlogicunit_1 (
    .TFRH_BUS(addressregister_1_tfer_buso[15:8]), .CLOCK(clockunit_1_clock_out),
    .TFRL_BUS(addressregister_1_tfer_buso[7:0]), .FLAGS_IN(flagsregister_1_oflags),
    .MAIN_BUS(pull_resistor_4_node), .FLAGS_OUT(arithmeticlogicunit_1_flags_out));  // open: ALU_CTL_BUS
  FlagsRegister flagsregister_1 (
    .OE(txbcontrolb_1_foe), .FLAGS(arithmeticlogicunit_1_flags_out), .CLOCK(clockunit_1_clock_out),
    .TFRL_BUS(addressregister_1_tfer_buso[7:0]), .OFLAGS(flagsregister_1_oflags));  // open: UPD
  TXBControlB txbcontrolb_1 (
    .TXBC(undriven_9), .BOL(txbcontrolb_1_bol), .BOH(txbcontrolb_1_boh), .BLD(txbcontrolb_1_bld),
    .COL(txbcontrolb_1_col), .COH(txbcontrolb_1_coh), .CLD(txbcontrolb_1_cld), .DOL(txbcontrolb_1_dol),
    .DOH(txbcontrolb_1_doh), .DLD(txbcontrolb_1_dld), .FOE(txbcontrolb_1_foe), .FLD(txbcontrolb_1_fld),
    .AOL(txbcontrolb_1_aol), .AOH(txbcontrolb_1_aoh), .ALD(txbcontrolb_1_ald));
  MBcontrol mbcontrol_1 (
    .MBC(undriven_8), .CLD(mbcontrol_1_cld), .DLD(mbcontrol_1_dld), .ALD(mbcontrol_1_ald),
    .BLD(mbcontrol_1_bld));

  // Notes on the sheet:
  //   Program Counter
  //   Transfer Register
  //   Interrupt Address Register
  //   DATA
  //   ADDR
  //   TFER
  //   MAIN
  //   General Purpose Registers
  //   Pipeline
endmodule

module ClockUnit (
  input  MANUAL_CLOCK,
  input  CLOCK_SELECT,
  output CLOCK_OUT,
  output INV_CLOCK_OUT
);

  wire and_1_out, and_2_out, clock_1_out, not_1_out;

  Clock clock_1 (.out(clock_1_out));
  not not_1 (not_1_out, CLOCK_SELECT);
  Pull_Resistor pull_resistor_1 (.node(CLOCK_SELECT));
  and and_1 (and_1_out, clock_1_out, not_1_out);
  and and_2 (and_2_out, MANUAL_CLOCK, CLOCK_SELECT);
  LED led_1 (.in(CLOCK_OUT));
  LED led_2 (.in(INV_CLOCK_OUT));
  or or_1 (CLOCK_OUT, and_1_out, and_2_out);
  not not_2 (INV_CLOCK_OUT, CLOCK_OUT);
endmodule

module AddressRegister (
  input  [15:0] TFER_BUS,
  input  INC,
  input  DEC,
  input  OADDR,
  input  OTFER,
  input  Load,
  input  CLOCK,
  output [15:0] ADDR_BUS,
  output [15:0] TFER_BUSO
);

  wire not_1_out, not_2_out, or_1_out, or_2_out;
  wire [15:0] adder_1_out, controlled_buffer_1_out, controlled_buffer_2_out, register_1_q;

  assign controlled_buffer_1_out = Load ? TFER_BUS : 16'bz;  // Controlled_Buffer controlled_buffer_1
  or or_1 (or_1_out, INC, DEC);
  assign controlled_buffer_2_out = INC ? 16'h1 : 16'bz;  // Controlled_Buffer controlled_buffer_2
  not not_1 (not_1_out, INC);
  assign controlled_buffer_2_out = not_1_out ? {16{1'b1}} : 16'bz;  // Controlled_Buffer controlled_buffer_3
  Register #(.width(16)) register_1 (
    .D(controlled_buffer_1_out), .en(or_2_out), .clk(not_2_out), .Q(register_1_q));  // open: clr
  or or_2 (or_2_out, or_1_out, Load);
  not not_2 (not_2_out, CLOCK);
  assign controlled_buffer_1_out = or_1_out ? adder_1_out : 16'bz;  // Controlled_Buffer controlled_buffer_4
  Adder #(.width(16)) adder_1 (.a(controlled_buffer_2_out), .b(register_1_q), .out(adder_1_out));  // open: cin, cout
  assign TFER_BUSO = OTFER ? register_1_q : 16'bz;  // Controlled_Buffer controlled_buffer_5
  assign ADDR_BUS = OADDR ? register_1_q : 16'bz;  // Controlled_Buffer controlled_buffer_6
endmodule

module GeneralPurposeRegister (
  input  [7:0] TFRL_BUS,
  input  [7:0] TFRH_BUS,
  input  [7:0] MAIN_BUS,
  input  TFRL,
  input  TFRH,
  input  TXLD,
  input  CLOCK,
  input  MBLD,
  output [7:0] TFRL_BUSO,
  output [7:0] TFRH_BUSO
);

  wire and_1_out, and_2_out, not_1_out, not_2_out, not_3_out, or_1_out;
  wire [7:0] controlled_buffer_1_out, controlled_buffer_4_out, controlled_buffer_5_out, register_1_q;

  not not_1 (not_1_out, TXLD);
  and and_1 (and_1_out, TFRL, not_1_out);
  or or_1 (or_1_out, TXLD, MBLD);
  and and_2 (and_2_out, not_1_out, TFRH);
  assign controlled_buffer_1_out = TFRL ? TFRL_BUS : 8'bz;  // Controlled_Buffer controlled_buffer_1
  assign controlled_buffer_1_out = TFRH ? TFRH_BUS : 8'bz;  // Controlled_Buffer controlled_buffer_2
  assign controlled_buffer_1_out = MBLD ? MAIN_BUS : 8'bz;  // Controlled_Buffer controlled_buffer_3
  Register register_1 (.D(controlled_buffer_4_out), .en(or_1_out), .clk(not_2_out), .Q(register_1_q));  // open: clr
  assign controlled_buffer_4_out = or_1_out ? controlled_buffer_1_out : 8'bz;  // Controlled_Buffer controlled_buffer_4
  not not_2 (not_2_out, CLOCK);
  assign controlled_buffer_5_out = not_3_out ? MAIN_BUS : 8'bz;  // Controlled_Buffer controlled_buffer_5
  not not_3 (not_3_out, MBLD);
  assign controlled_buffer_5_out = not_3_out ? register_1_q : 8'bz;  // Controlled_Buffer controlled_buffer_6
  assign TFRH_BUSO = and_2_out ? controlled_buffer_5_out : 8'bz;  // Controlled_Buffer controlled_buffer_7
  assign TFRL_BUSO = and_1_out ? controlled_buffer_5_out : 8'bz;  // Controlled_Buffer controlled_buffer_8
endmodule

module ArithmeticLogicUnit (
  input  [7:0] TFRL_BUS,
  input  [7:0] TFRH_BUS,
  input  [3:0] ALU_CTL_BUS,
  input  CLOCK,
  input  [7:0] FLAGS_IN,
  output [7:0] MAIN_BUS,
  output [7:0] FLAGS_OUT
);

  wire multiplexer_1_out, multiplexer_2_out;
  wire [1:0] aludecode_1_carry_sel, aludecode_1_shift_sel;
  wire [3:0] aludecode_1_bitwise_sel;
  wire [7:0] logicunit_1_lu_out, register_1_q, register_2_q, shiftunit_1_su_out;

  Multiplexer #(.select(2)) multiplexer_1 (
    .in0(1'b0), .in1(FLAGS_IN[1]), .in2(1'b1), .in3(1'b0), .out(multiplexer_1_out),
    .sel(aludecode_1_carry_sel));
  ShiftUnit shiftunit_1 (
    .SFT_CODE(aludecode_1_shift_sel), .CARRY_IN(multiplexer_1_out), .LHS(TFRL_BUS), .CARRY_OUT(FLAGS_OUT[1]),
    .SU_OUT(shiftunit_1_su_out));
  LogicUnit logicunit_1 (.OP_LUT(aludecode_1_bitwise_sel), .LHS(TFRL_BUS), .RHS(TFRH_BUS), .LU_OUT(logicunit_1_lu_out));
  ALUDecode aludecode_1 (
    .ALU_INST(ALU_CTL_BUS), .CARRY_SEL(aludecode_1_carry_sel), .SHIFT_SEL(aludecode_1_shift_sel),
    .BITWISE_SEL(aludecode_1_bitwise_sel));
  Register register_1 (.D(shiftunit_1_su_out), .en(1'b1), .clk(CLOCK), .Q(register_1_q));  // open: clr
  Register register_2 (.D(logicunit_1_lu_out), .en(1'b1), .clk(CLOCK), .Q(register_2_q));  // open: clr
  Multiplexer #(.select(2)) multiplexer_2 (
    .in0(1'b0), .in1(FLAGS_IN[0]), .in2(1'b1), .in3(1'b0), .out(multiplexer_2_out),
    .sel(aludecode_1_carry_sel));
  Adder adder_1 (.a(register_1_q), .b(register_2_q), .out(MAIN_BUS), .cin(multiplexer_2_out), .cout(FLAGS_OUT[0]));
endmodule

module ALUDecode (
  input  [3:0] ALU_INST,
  output [1:0] CARRY_SEL,
  output [1:0] SHIFT_SEL,
  output [3:0] BITWISE_SEL
);

  ROM #(.addrWidth(4)) rom_1 (.addr(ALU_INST), .data({BITWISE_SEL, SHIFT_SEL, CARRY_SEL}));

  // Notes on the sheet:
  //   contents of rom_1 (hex, n*v repeats v):
  //   0 c 4c 83 43 80 40 f 4f 10 20 33 38 3e 36
endmodule

module LogicUnit (
  input  [7:0] LHS,
  input  [7:0] RHS,
  input  [3:0] OP_LUT,
  output [7:0] LU_OUT
);

  Multiplexer #(.select(2)) multiplexer_1 (
    .in0(OP_LUT[0]), .in1(OP_LUT[1]), .in2(OP_LUT[2]), .in3(OP_LUT[3]), .out(LU_OUT[0]),
    .sel({RHS[0], LHS[0]}));
  Multiplexer #(.select(2)) multiplexer_2 (
    .in0(OP_LUT[0]), .in1(OP_LUT[1]), .in2(OP_LUT[2]), .in3(OP_LUT[3]), .out(LU_OUT[1]),
    .sel({RHS[1], LHS[1]}));
  Multiplexer #(.select(2)) multiplexer_3 (
    .in0(OP_LUT[0]), .in1(OP_LUT[1]), .in2(OP_LUT[2]), .in3(OP_LUT[3]), .out(LU_OUT[2]),
    .sel({RHS[2], LHS[2]}));
  Multiplexer #(.select(2)) multiplexer_4 (
    .in0(OP_LUT[0]), .in1(OP_LUT[1]), .in2(OP_LUT[2]), .in3(OP_LUT[3]), .out(LU_OUT[3]),
    .sel({RHS[3], LHS[3]}));
  Multiplexer #(.select(2)) multiplexer_5 (
    .in0(OP_LUT[0]), .in1(OP_LUT[1]), .in2(OP_LUT[2]), .in3(OP_LUT[3]), .out(LU_OUT[4]),
    .sel({RHS[4], LHS[4]}));
  Multiplexer #(.select(2)) multiplexer_6 (
    .in0(OP_LUT[0]), .in1(OP_LUT[1]), .in2(OP_LUT[2]), .in3(OP_LUT[3]), .out(LU_OUT[5]),
    .sel({RHS[5], LHS[5]}));
  Multiplexer #(.select(2)) multiplexer_7 (
    .in0(OP_LUT[0]), .in1(OP_LUT[1]), .in2(OP_LUT[2]), .in3(OP_LUT[3]), .out(LU_OUT[6]),
    .sel({RHS[6], LHS[6]}));
  Multiplexer #(.select(2)) multiplexer_8 (
    .in0(OP_LUT[0]), .in1(OP_LUT[1]), .in2(OP_LUT[2]), .in3(OP_LUT[3]), .out(LU_OUT[7]),
    .sel({RHS[7], LHS[7]}));
endmodule

module ShiftUnit (
  input  [7:0] LHS,
  input  [1:0] SFT_CODE,
  input  CARRY_IN,
  output [7:0] SU_OUT,
  output CARRY_OUT
);

  wire demultiplexer_1_out0, demultiplexer_1_out1, demultiplexer_1_out2, demultiplexer_1_out3;

  Demultiplexer #(.select(2)) demultiplexer_1 (
    .out0(demultiplexer_1_out0), .out1(demultiplexer_1_out1), .out2(demultiplexer_1_out2),
    .out3(demultiplexer_1_out3), .in(1'b1), .sel(SFT_CODE));
  assign SU_OUT = demultiplexer_1_out3 ? {8{1'b0}} : 8'bz;  // Controlled_Buffer controlled_buffer_1
  assign SU_OUT = demultiplexer_1_out2 ? {CARRY_IN, LHS[7:1]} : 8'bz;  // Controlled_Buffer controlled_buffer_2
  assign SU_OUT = demultiplexer_1_out1 ? {LHS[6:1], LHS[7], CARRY_IN} : 8'bz;  // Controlled_Buffer controlled_buffer_3
  assign SU_OUT = demultiplexer_1_out0 ? {LHS[7:1], LHS[7]} : 8'bz;  // Controlled_Buffer controlled_buffer_4

  assign CARRY_OUT = LHS[7];
  assign LHS[0] = LHS[7];
endmodule

module MemoryUnit (
  input  [15:0] ADDR_BUS,
  input  RWB,
  input  CLOCK,
  output [7:0] DATA_BUS
);

  ROM #(.addrWidth(16)) rom_1 (.addr(ADDR_BUS), .data(DATA_BUS));
  RAM ram_1 ();  // open: addr, we, oe, clk, din, dout
endmodule

module MemoryBridge (
  input  [7:0] DATA_BUS,
  input  [7:0] TFRL_BUS,
  input  LOAD,
  input  STORE,
  output [7:0] OTFRL_BUS,
  output [7:0] ODATA_BUS
);

  assign OTFRL_BUS = LOAD ? DATA_BUS : 8'bz;  // Controlled_Buffer controlled_buffer_1
  assign ODATA_BUS = STORE ? TFRL_BUS : 8'bz;  // Controlled_Buffer controlled_buffer_2
endmodule

module FlagsRegister (
  input  OE,
  input  [7:0] FLAGS,
  input  UPD,
  input  CLOCK,
  output [7:0] TFRL_BUS,
  output [7:0] OFLAGS
);

  Register register_1 (.D(FLAGS), .en(UPD), .clk(CLOCK), .Q(OFLAGS));  // open: clr
  LED led_1 (.in(OFLAGS[7]));
  LED led_2 (.in(OFLAGS[6]));
  LED led_3 (.in(OFLAGS[5]));
  assign TFRL_BUS = OE ? OFLAGS : 8'bz;  // Controlled_Buffer controlled_buffer_1
  LED led_4 (.in(OFLAGS[4]));
  LED led_5 (.in(OFLAGS[3]));
  LED led_6 (.in(OFLAGS[2]));
  LED led_7 (.in(OFLAGS[1]));
  LED led_8 (.in(OFLAGS[0]));
endmodule

module Stack (
  input  [15:0] TFER_BUS,
  input  CLOCK,
  input  PUSH,
  input  POP,
  output [15:0] OTFER_BUS
);

  wire d_ff_1_q;
  wire [7:0] ram_1_dout, ram_2_dout, stackpointer_1_addr;

  StackPointer stackpointer_1 (.INC(PUSH), .DEC(POP), .CLOCK(CLOCK), .ADDR(stackpointer_1_addr));
  D_Flip_Flop d_ff_1 (.D(POP), .clk(CLOCK), .Q(d_ff_1_q));  // open: Qn, preset, reset
  RAM ram_1 (.addr(stackpointer_1_addr), .we(PUSH), .oe(POP), .clk(CLOCK), .din(TFER_BUS[7:0]), .dout(ram_1_dout));
  RAM ram_2 (.addr(stackpointer_1_addr), .we(PUSH), .oe(POP), .clk(CLOCK), .din(TFER_BUS[15:8]), .dout(ram_2_dout));
  assign OTFER_BUS = d_ff_1_q ? {ram_2_dout, ram_1_dout} : 16'bz;  // Controlled_Buffer controlled_buffer_1
endmodule

module StackPointer (
  input  INC,
  input  DEC,
  input  CLOCK,
  output [7:0] ADDR
);

  wire not_1_out, not_2_out, or_1_out;
  wire [7:0] adder_1_out, controlled_buffer_1_out, controlled_buffer_3_out;

  or or_1 (or_1_out, INC, DEC);
  assign controlled_buffer_1_out = INC ? 8'h1 : 8'bz;  // Controlled_Buffer controlled_buffer_1
  not not_1 (not_1_out, INC);
  assign controlled_buffer_1_out = not_1_out ? {8{1'b1}} : 8'bz;  // Controlled_Buffer controlled_buffer_2
  Register register_1 (.D(controlled_buffer_3_out), .en(or_1_out), .clk(not_2_out), .Q(ADDR));  // open: clr
  not not_2 (not_2_out, CLOCK);
  assign controlled_buffer_3_out = or_1_out ? adder_1_out : 8'bz;  // Controlled_Buffer controlled_buffer_3
  Adder adder_1 (.a(controlled_buffer_1_out), .b(ADDR), .out(adder_1_out));  // open: cin, cout
endmodule

module TXBControlA (
  input  [7:0] TXBC,
  output PCTOE,
  output PCLD,
  output TXTOE,
  output TXLD,
  output IATOE,
  output IALD,
  output SPUSH,
  output SPOP
);

  wire controlled_buffer_1_out, demultiplexer_1_out0, demultiplexer_1_out1, demultiplexer_1_out2,
       demultiplexer_1_out3;
  wire [5:0] controlled_buffer_2_out, controlled_buffer_3_out, controlled_buffer_4_out;

  Demultiplexer #(.select(2)) demultiplexer_1 (
    .out0(demultiplexer_1_out0), .out1(demultiplexer_1_out1), .out2(demultiplexer_1_out2),
    .out3(demultiplexer_1_out3), .in(1'b1), .sel(TXBC[7:6]));
  assign controlled_buffer_1_out = demultiplexer_1_out0 ? 1'b0 : 1'bz;  // Controlled_Buffer controlled_buffer_1
  assign controlled_buffer_2_out = demultiplexer_1_out1 ? TXBC[5:0] : 6'bz;  // Controlled_Buffer controlled_buffer_2
  assign controlled_buffer_3_out = demultiplexer_1_out2 ? TXBC[5:0] : 6'bz;  // Controlled_Buffer controlled_buffer_3
  assign controlled_buffer_4_out = demultiplexer_1_out3 ? TXBC[5:0] : 6'bz;  // Controlled_Buffer controlled_buffer_4
  Demultiplexer #(.select(3)) demultiplexer_2 (
    .in(1'b1), .sel(controlled_buffer_2_out[2:0]));  // open: out0, out1, out2, out3, out4, out5, out6, out7
  Demultiplexer #(.select(3)) demultiplexer_3 (
    .in(1'b1), .sel(controlled_buffer_2_out[5:3]));  // open: out0, out1, out2, out3, out4, out5, out6, out7
  Demultiplexer #(.select(2)) demultiplexer_4 (
    .out2(TXTOE), .out3(SPOP), .in(1'b1), .sel(controlled_buffer_3_out[5:4]));  // open: out0, out1
  Demultiplexer #(.select(2)) demultiplexer_5 (
    .out2(TXLD), .out3(SPUSH), .in(1'b1), .sel(controlled_buffer_3_out[3:2]));  // open: out0, out1
  Demultiplexer #(.select(2)) demultiplexer_6 (
    .out0(IATOE), .out1(SPOP), .out2(TXTOE), .out3(PCTOE), .in(1'b1), .sel(controlled_buffer_4_out[5:4]));
  Demultiplexer #(.select(2)) demultiplexer_7 (
    .out0(IALD), .out1(SPUSH), .out2(TXLD), .out3(PCLD), .in(1'b1), .sel(controlled_buffer_4_out[3:2]));
  Pull_Resistor pull_resistor_1 (.node({PCTOE, PCLD, TXTOE, TXLD, IATOE, IALD, SPUSH, SPOP}));
endmodule

module TXBControlB (
  input  [7:0] TXBC,
  output AOL,
  output AOH,
  output ALD,
  output BOL,
  output BOH,
  output BLD,
  output COL,
  output COH,
  output CLD,
  output DOL,
  output DOH,
  output DLD,
  output FOE,
  output FLD
);

  wire controlled_buffer_1_out, demultiplexer_1_out0, demultiplexer_1_out1, demultiplexer_1_out2,
       demultiplexer_1_out3;
  wire [5:0] controlled_buffer_2_out, controlled_buffer_3_out, controlled_buffer_4_out;

  Demultiplexer #(.select(2)) demultiplexer_1 (
    .out0(demultiplexer_1_out0), .out1(demultiplexer_1_out1), .out2(demultiplexer_1_out2),
    .out3(demultiplexer_1_out3), .in(1'b1), .sel(TXBC[7:6]));
  assign controlled_buffer_1_out = demultiplexer_1_out0 ? 1'b0 : 1'bz;  // Controlled_Buffer controlled_buffer_1
  assign controlled_buffer_2_out = demultiplexer_1_out1 ? TXBC[5:0] : 6'bz;  // Controlled_Buffer controlled_buffer_2
  assign controlled_buffer_3_out = demultiplexer_1_out2 ? TXBC[5:0] : 6'bz;  // Controlled_Buffer controlled_buffer_3
  assign controlled_buffer_4_out = demultiplexer_1_out3 ? TXBC[5:0] : 6'bz;  // Controlled_Buffer controlled_buffer_4
  Demultiplexer #(.select(3)) demultiplexer_2 (
    .out0(AOL), .out1(BOL), .out2(COL), .out3(DOL), .out4(FOE), .in(1'b1), .sel(controlled_buffer_2_out[2:0]));  // open: out5, out6, out7
  Demultiplexer #(.select(3)) demultiplexer_3 (
    .out0(ALD), .out1(BLD), .out2(CLD), .out3(DLD), .out4(FLD), .in(1'b1), .sel(controlled_buffer_2_out[5:3]));  // open: out5, out6, out7
  Demultiplexer #(.select(3)) demultiplexer_4 (
    .out0(AOL), .out1(BOL), .out2(COL), .out3(DOL), .in(1'b1), .sel(controlled_buffer_2_out[5:3]));  // open: out4, out5, out6, out7
  Demultiplexer #(.select(2)) demultiplexer_5 (
    .out0(AOL), .out1(COL), .in(1'b1), .sel(controlled_buffer_3_out[5:4]));  // open: out2, out3
  Demultiplexer #(.select(2)) demultiplexer_6 (
    .out0(AOL), .out1(COL), .in(1'b1), .sel(controlled_buffer_3_out[3:2]));  // open: out2, out3
  Demultiplexer #(.select(2)) demultiplexer_7 (
    .out0(BOH), .out1(DOH), .in(1'b1), .sel(controlled_buffer_3_out[5:4]));  // open: out2, out3
  Demultiplexer #(.select(2)) demultiplexer_8 (
    .out0(BOH), .out1(DOH), .in(1'b1), .sel(controlled_buffer_3_out[3:2]));  // open: out2, out3
  Demultiplexer #(.select(2)) demultiplexer_9 (
    .out0(ALD), .out1(CLD), .in(1'b1), .sel(controlled_buffer_3_out[3:2]));  // open: out2, out3
  Demultiplexer #(.select(2)) demultiplexer_10 (
    .out0(BLD), .out1(DLD), .in(1'b1), .sel(controlled_buffer_3_out[3:2]));  // open: out2, out3
  Demultiplexer #(.select(2)) demultiplexer_11 (
    .in(1'b1), .sel(controlled_buffer_4_out[5:4]));  // open: out0, out1, out2, out3
  Demultiplexer #(.select(2)) demultiplexer_12 (
    .in(1'b1), .sel(controlled_buffer_4_out[3:2]));  // open: out0, out1, out2, out3
  Pull_Resistor pull_resistor_1 (.node({AOL, AOH, ALD, BOL, BOH, BLD, COL, COH, CLD, DOL, DOH, DLD, FOE, FLD}));
endmodule

module MBcontrol (
  input  [2:0] MBC,
  output ALD,
  output BLD,
  output CLD,
  output DLD
);

  Demultiplexer #(.select(2)) demultiplexer_1 (
    .out0(ALD), .out1(BLD), .out2(CLD), .out3(DLD), .in(MBC[0]), .sel(MBC[2:1]));
endmodule
